# Fritzing sketch schematicSource (saved by Fritzing 0.9.3b)
breadboards: 1

parts:
  Part1 = Arduino Uno (Rev3)
  LED1 = LED - 5mm [color="Red (633nm)" package="5 mm [THT]"]
  LED2 = LED - 5mm [color="Yellow (585nm)" package="5 mm [THT]"]
  LED3 = LED - 5mm [color="Green (555nm)" package="5 mm [THT]"]
  R1 = Resistor [tolerance=±5% resistance=470 package=THT]
  R2 = Resistor [tolerance=±5% resistance=470 package=THT]
  R3 = Resistor [tolerance=±5% resistance=470 package=THT]
  Part2 = SRF05 Ultrasonic Rangefinder

nets:
  N1: Part1.D8, LED1.anode
  N2: Part1.D9_PWM, LED2.anode
  N3: Part1.D10_PWM/SS, LED3.anode
  GND: Part1.GND, R1.Pin_1, R2.Pin_1, R3.Pin_1, Part2.GND
  N4: Part1.D3_PWM, Part2.Echo
  N5: Part1.D4, Part2.Trig
  5V: Part1.5V, Part2.VCC
  N6: LED1.cathode, R3.Pin_0
  N7: LED2.cathode, R2.Pin_0
  N8: LED3.cathode, R1.Pin_0
